// Logisim project hell_outside.circ as structural Verilog: 5 circuits, main circuit main
module registradores (
  input  [3:0] RS,
  input  REG_Write,
  input  [3:0] RD,
  input  [3:0] RT,
  input  [15:0] oque,
  input  clock,
  output [15:0] REG3,
  output [15:0] Data_RS,
  output [15:0] Data_RT
);

  wire demultiplexer_1_out0, demultiplexer_1_out1, demultiplexer_1_out2, demultiplexer_1_out3,
       demultiplexer_1_out4, demultiplexer_1_out5, demultiplexer_1_out6, demultiplexer_1_out7,
       demultiplexer_1_out8, demultiplexer_1_out9, demultiplexer_1_out10, demultiplexer_1_out11,
       demultiplexer_1_out12, demultiplexer_1_out13, demultiplexer_1_out14, demultiplexer_1_out15;
  wire [15:0] register_1_q, register_3_q, register_4_q, register_5_q, register_6_q, register_7_q,
       register_8_q, register_9_q, register_10_q, register_11_q, register_12_q, register_13_q, register_14_q,
       t0_q, zero_q;

  Demultiplexer #(.select(4)) demultiplexer_1 (
    .out0(demultiplexer_1_out0), .out1(demultiplexer_1_out1), .out2(demultiplexer_1_out2),
    .out3(demultiplexer_1_out3), .out4(demultiplexer_1_out4), .out5(demultiplexer_1_out5),
    .out6(demultiplexer_1_out6), .out7(demultiplexer_1_out7), .out8(demultiplexer_1_out8),
    .out9(demultiplexer_1_out9), .out10(demultiplexer_1_out10), .out11(demultiplexer_1_out11),
    .out12(demultiplexer_1_out12), .out13(demultiplexer_1_out13), .out14(demultiplexer_1_out14),
    .out15(demultiplexer_1_out15), .in(REG_Write), .sel(RD));  // open: en
  Register #(.width(16)) zero (.D(oque), .Q(zero_q), .clk(clock), .clr(1'b1));  // open: en
  Register #(.width(16)) t0 (.D(oque), .en(demultiplexer_1_out1), .Q(t0_q), .clk(clock));  // open: clr
  Register #(.width(16)) register_1 (.D(oque), .en(demultiplexer_1_out2), .Q(register_1_q), .clk(clock));  // open: clr
  Register #(.width(16)) register_2 (.D(oque), .en(demultiplexer_1_out3), .Q(REG3), .clk(clock));  // open: clr
  Register #(.width(16)) register_3 (.D(oque), .en(demultiplexer_1_out4), .Q(register_3_q), .clk(clock));  // open: clr
  Register #(.width(16)) register_4 (.D(oque), .en(demultiplexer_1_out5), .Q(register_4_q), .clk(clock));  // open: clr
  Register #(.width(16)) register_5 (.D(oque), .en(demultiplexer_1_out6), .Q(register_5_q), .clk(clock));  // open: clr
  Register #(.width(16)) register_6 (.D(oque), .en(demultiplexer_1_out7), .Q(register_6_q), .clk(clock));  // open: clr
  Register #(.width(16)) register_7 (.D(oque), .en(demultiplexer_1_out11), .Q(register_7_q), .clk(clock));  // open: clr
  Register #(.width(16)) register_8 (.D(oque), .en(demultiplexer_1_out12), .Q(register_8_q), .clk(clock));  // open: clr
  Register #(.width(16)) register_9 (.D(oque), .en(demultiplexer_1_out13), .Q(register_9_q), .clk(clock));  // open: clr
  Register #(.width(16)) register_10 (
    .D(oque), .en(demultiplexer_1_out14), .Q(register_10_q), .clk(clock));  // open: clr
  Register #(.width(16)) register_11 (
    .D(oque), .en(demultiplexer_1_out15), .Q(register_11_q), .clk(clock));  // open: clr
  Register #(.width(16)) register_12 (
    .D(oque), .en(demultiplexer_1_out8), .Q(register_12_q), .clk(clock));  // open: clr
  Register #(.width(16)) register_13 (
    .D(oque), .en(demultiplexer_1_out9), .Q(register_13_q), .clk(clock));  // open: clr
  Register #(.width(16)) register_14 (
    .D(oque), .en(demultiplexer_1_out10), .Q(register_14_q), .clk(clock));  // open: clr
  Multiplexer #(.select(4), .width(16)) multiplexer_1 (
    .in0(zero_q), .in1(t0_q), .in2(register_1_q), .in3(REG3), .in4(register_3_q), .in5(register_4_q),
    .in6(register_5_q), .in7(register_6_q), .in8(register_12_q), .in9(register_13_q), .in10(register_14_q),
    .in11(register_7_q), .in12(register_8_q), .in13(register_9_q), .in14(register_10_q),
    .in15(register_11_q), .out(Data_RS), .sel(RS));  // open: en
  Multiplexer #(.select(4), .width(16)) multiplexer_2 (
    .in0(zero_q), .in1(t0_q), .in2(register_1_q), .in3(REG3), .in4(register_3_q), .in5(register_4_q),
    .in6(register_5_q), .in7(register_6_q), .in8(register_12_q), .in9(register_13_q), .in10(register_14_q),
    .in11(register_7_q), .in12(register_8_q), .in13(register_9_q), .in14(register_10_q),
    .in15(register_11_q), .out(Data_RT), .sel(RT));  // open: en
endmodule

// write reg
module main (
  input  in_1,
  output regWrite,
  output aluSrc,
  output regdst,
  output memRead,
  output [2:0] aluop,
  output branch,
  output memtoreg,
  output memWrite,
  output jump,
  output [15:0] out_11,
  output [3:0] RS,
  output [15:0] Data_rs,
  output [3:0] RT,
  output [3:0] RD,
  output [15:0] DATa_RT,
  output [3:0] _0_3,
  output [15:0] oque_escrevo,
  output [3:0] _4_7,
  output [3:0] opcode_12_15,
  output [3:0] _8_11
);

  wire alu_1_beq, and_1_out, clock_1_out, comparator_1_eq;
  wire [3:0] multiplexer_1_out;
  wire [7:0] adder_1_out, multiplexer_3_out, Pc_q;
  wire [15:0] alu_1_alu_resul, counter_1_q, extensor_4_16_out_2, multiplexer_2_out, ram_2_data;

  Clock clock_1 (.out(clock_1_out));
  Register Pc (.D(multiplexer_3_out), .Q(Pc_q), .clk(clock_1_out), .clr(in_1));  // open: en
  Adder adder_1 (.a(8'h1), .b(Pc_q), .out(adder_1_out));  // open: cin, cout
  Hex_Digit_Display hex_digit_display_1 (.value(out_11[15:12]));  // open: dp
  RAM #(.dataWidth(16)) ram_1 (.addr(Pc_q), .data({opcode_12_15, _8_11, _4_7, _0_3}));  // open: sel, clk, ld, clr
  Hex_Digit_Display hex_digit_display_2 (.value(out_11[11:8]));  // open: dp
  Hex_Digit_Display hex_digit_display_3 (.value(out_11[3:0]));  // open: dp
  Hex_Digit_Display hex_digit_display_4 (.value(out_11[7:4]));  // open: dp
  unidade_de_controle unidade_de_controle_1 (
    .zero(opcode_12_15[0]), .um(opcode_12_15[1]), .dois(opcode_12_15[2]), .tres(opcode_12_15[3]),
    .regWrite(regWrite), .regdst(regdst), .aluSrc(aluSrc), .aluop(aluop), .memRead(memRead), .branch(branch),
    .jump(jump), .memWrite(memWrite), .memtoreg(memtoreg));  // open: a
  Multiplexer #(.width(4), .enable("false")) multiplexer_1 (
    .in0(_4_7), .in1(_0_3), .out(multiplexer_1_out), .sel(regdst));
  extenso_de_sinal extensor_4_16 (.in_1(_0_3), .out_2(extensor_4_16_out_2));
  registradores registradores_1 (
    .Data_RS(Data_rs), .Data_RT(DATa_RT), .oque(oque_escrevo), .REG_Write(regWrite), .RS(_8_11), .RT(_4_7),
    .clock(clock_1_out), .RD(multiplexer_1_out), .REG3(out_11));
  Multiplexer #(.width(16), .enable("false")) multiplexer_2 (
    .in0(DATa_RT), .in1(extensor_4_16_out_2), .out(multiplexer_2_out), .sel(aluSrc));
  and and_1 (and_1_out, branch, alu_1_beq);
  ALU alu_1 (.A(Data_rs), .B(multiplexer_2_out), .ALU_RESUL(alu_1_alu_resul), .ALUOp(aluop), .BEQ(alu_1_beq));
  Comparator #(.width(4)) comparator_1 (.a(opcode_12_15), .b(4'b1111), .eq(comparator_1_eq));  // open: gt, lt
  Multiplexer #(.width(8), .enable("false")) multiplexer_3 (
    .in0(adder_1_out), .in1({4'b0000, _0_3}), .out(multiplexer_3_out), .sel(and_1_out));
  Counter #(.width(16), .max('hffff)) counter_1 (
    .D(16'h1), .Q(counter_1_q), .clk(comparator_1_eq), .clr(in_1));  // open: load, count, carry
  RAM #(.addrWidth(16), .dataWidth(16), .bus("separate")) ram_2 (
    .addr(counter_1_q), .din(DATa_RT), .data(ram_2_data), .str(memWrite), .clk(clock_1_out), .ld(memRead));  // open: sel, clr
  Multiplexer #(.width(16), .enable("false")) multiplexer_4 (
    .in0(alu_1_alu_resul), .in1(ram_2_data), .out(oque_escrevo), .sel(memtoreg));

  assign RD = _0_3;
  assign RS = _8_11;
  assign RT = _4_7;

  // Other names for the same wires on the sheet: teste[3:0] = _0_3; OPCODE[3:0] = opcode_12_15
endmodule

module unidade_de_controle (
  input  zero,
  input  um,
  input  dois,
  input  tres,
  output regWrite,
  output regdst,
  output aluSrc,
  output a,
  output [2:0] aluop,
  output memRead,
  output branch,
  output jump,
  output memWrite,
  output memtoreg
);

  wire and_1_out, and_2_out, and_3_out, and_4_out, and_5_out, and_7_out, and_8_out, and_9_out, not_1_out,
       not_2_out, not_3_out, not_4_out, not_5_out, not_6_out, not_7_out, not_8_out, not_9_out, not_10_out,
       not_11_out, not_12_out, not_13_out, not_14_out, not_15_out, not_16_out;

  not not_1 (not_1_out, dois);
  not not_2 (not_2_out, zero);
  not not_3 (not_3_out, zero);
  not not_4 (not_4_out, um);
  not not_5 (not_5_out, tres);
  not not_6 (not_6_out, zero);
  not not_7 (not_7_out, dois);
  not not_8 (not_8_out, dois);
  not not_9 (not_9_out, zero);
  not not_10 (not_10_out, zero);
  not not_11 (not_11_out, dois);
  not not_12 (not_12_out, um);
  not not_13 (not_13_out, um);
  not not_14 (not_14_out, zero);
  not not_15 (not_15_out, um);
  not not_16 (not_16_out, zero);
  or or_1 (regWrite, not_1_out, not_2_out, um);
  and and_1 (and_1_out, not_3_out, not_4_out, not_5_out);
  and and_2 (and_2_out, not_6_out, not_7_out);
  and and_3 (and_3_out, zero, um, dois);
  and and_4 (and_4_out, not_8_out, zero);
  and and_5 (and_5_out, dois, um, not_9_out);
  and and_6 (memRead, dois, um, not_10_out);
  and and_7 (and_7_out, not_11_out, um);
  and and_8 (and_8_out, dois, not_12_out);
  and and_9 (and_9_out, dois, zero);
  and and_10 (aluop[2], dois, not_13_out, not_14_out);
  and and_11 (branch, dois, not_15_out, zero);
  and and_12 (memtoreg, dois, um, not_16_out);
  or or_2 (regdst, and_1_out, and_2_out, and_3_out);
  or or_3 (aluSrc, and_4_out, and_5_out);
  or or_4 (aluop[0], and_7_out, and_8_out, and_9_out);

  assign a = tres;
  assign aluop[1] = 1'b0;
  assign jump = 1'b0;
  assign memWrite = 1'b0;
endmodule

module ALU (
  input  [15:0] A,
  input  [15:0] B,
  input  [2:0] ALUOp,
  output BEQ,
  output [15:0] ALU_RESUL
);

  wire and_1_out, comparator_1_lt, comparator_2_eq;
  wire [15:0] adder_1_out, multiplexer_1_out, multiplexer_2_out, subtractor_1_out;

  Comparator #(.width(16)) comparator_1 (.a(A), .b(B), .lt(comparator_1_lt));  // open: gt, eq
  Adder #(.width(16)) adder_1 (.a(A), .b(B), .out(adder_1_out));  // open: cin, cout
  Subtractor #(.width(16)) subtractor_1 (.a(A), .b(B), .out(subtractor_1_out));  // open: bin, bout
  Multiplexer #(.width(16), .enable("false")) multiplexer_1 (
    .in0({16{1'b0}}), .in1(16'h1), .out(multiplexer_1_out), .sel(comparator_1_lt));
  Multiplexer #(.select(3), .width(16), .enable("false")) multiplexer_2 (
    .in0(adder_1_out), .in1(subtractor_1_out), .out(multiplexer_2_out), .sel(ALUOp));  // open: in2, in3, in4, in5, in6, in7
  Comparator #(.width(3)) comparator_2 (.a(ALUOp), .b(3'b101), .eq(comparator_2_eq));  // open: gt, lt
  Multiplexer #(.width(16), .enable("false")) multiplexer_3 (
    .in0(multiplexer_2_out), .in1(multiplexer_1_out), .out(ALU_RESUL), .sel(comparator_2_eq));
  not not_1 (BEQ, and_1_out);
  and and_1 (and_1_out, ~multiplexer_2_out[0], ~multiplexer_2_out[1], ~multiplexer_2_out[2], ~multiplexer_2_out[3], ~multiplexer_2_out[4], ~multiplexer_2_out[5], ~multiplexer_2_out[6], ~multiplexer_2_out[7], ~multiplexer_2_out[8], ~multiplexer_2_out[9], ~multiplexer_2_out[10], ~multiplexer_2_out[11], ~multiplexer_2_out[12], ~multiplexer_2_out[13], ~multiplexer_2_out[14], ~multiplexer_2_out[15]);  // AND_Gate
endmodule

module extenso_de_sinal (
  input  [3:0] in_1,
  output [15:0] out_2
);


  assign out_2 = {{12{1'b0}}, in_1};
endmodule
